// Logisim project ADD_4.circ as structural Verilog: 3 circuits, main circuit main
module main (
  input  [3:0] in_1,
  input  [3:0] in_2,
  output out_3,
  output [3:0] out_4
);

  // Probe on in_1
  ADD4 add4_1 (.A(in_1), .B(in_2), .out_4(out_4), .Overflow(out_3));
  // Probe on in_2
  // Probe on out_4
endmodule

module ADD4 (
  input  [3:0] B,
  input  [3:0] A,
  output Overflow,
  output [3:0] out_4
);

  wire add1_2_vai_1, add1_3_vai_1, add1_4_vai_1;

  ADD1 add1_1 (.S(out_4[3]), .Vai_1(Overflow), .A(A[3]), .B(B[3]), .Vem_1(add1_2_vai_1));
  ADD1 add1_2 (.S(out_4[2]), .Vai_1(add1_2_vai_1), .A(A[2]), .B(B[2]), .Vem_1(add1_3_vai_1));
  ADD1 add1_3 (.S(out_4[1]), .Vai_1(add1_3_vai_1), .A(A[1]), .B(B[1]), .Vem_1(add1_4_vai_1));
  ADD1 add1_4 (.S(out_4[0]), .Vai_1(add1_4_vai_1), .A(A[0]), .B(B[0]), .Vem_1(1'b0));
endmodule

module ADD1 (
  input  A,
  input  B,
  input  Vem_1,
  output S,
  output Vai_1
);

  wire and_1_out, and_2_out, or_1_out, xor_1_out;

  xor xor_1 (xor_1_out, B, A);
  or or_1 (or_1_out, Vem_1, B);
  and and_1 (and_1_out, B, Vem_1);
  xor xor_2 (S, Vem_1, xor_1_out);
  and and_2 (and_2_out, or_1_out, A);
  or or_2 (Vai_1, and_2_out, and_1_out);
endmodule
